# Fritzing sketch HamsterFeeder (saved by Fritzing 0.9.3b)

parts:
  part = ESP32-38PinWide [part_number=ESP32-38PinWide]
  part_2 = 28BYJ-48 Stepper Motor [part_number=28BYJ-48]
  part_3 = 28BYJ-48 Driver Module [part_number=ULN2003 package=THT]
  USB-A_(Female) = USB Connectors [package=usb-a-h]
  SEN0297 = CAPSENSE_PAD [package=capsense_pad]
  R1 = Resistor [tolerance=±5% resistance=220 package=THT]

nets:
  N1: part.GPIO35, part_3.IN1
  N2: part.GPIO32, part_3.IN2
  N3: part.GPIO33, part_3.IN3
  N4: part.GPIO25, part_3.IN4
  N5: part.GPIO9, SEN0297.RECEIVE
  GND: part.GPIO11, part_3.GND, USB-A_(Female).GND, R1.Pin_0
  N6: part.VIN, part_3.Vmotor, USB-A_(Female).VBUS
  N7: part_2.blue-pin, part_3.blue-pin
  N8: part_2.pink-pin, part_3.pink-pin
  N9: part_2.yellow-pin, part_3.yellow-pin
  N10: part_2.orange-pin, part_3.orange-pin
  N11: part_2.red-pin, part_3.red-pin

custom parts:
  ESP32-38PinWide: Generic 38-Pin ESP32 with wide format (only access to one side of pins on a breadboard) based on Stephen Lilley's HiLetgo ESP-WROOM-32 ESP32 ESP-32S Development Board.
  28BYJ-48 Stepper Motor: Unipolar Stepper Motor 28BYJ-48 Top coil - pink & orange Bottom coil - blue & yellow Common rail - red Connector pins: blue - pink - yellow - orange - red
  28BYJ-48 Driver Module: ULN2003 Driver Module for the 28BYJ-48 Unipolar Stepper Motor LED A - Blue wire - Bottom coil left LED B - Pink wire - Top coil left LED C - Yellow wire - Bottom coil right LED D - Orange wire - Top coil right Common rail - red Connector pins: blue - pink - yellow - orange - red Control pins - IN1 to IN4 Power pins - GND & Vmotor (5-12V) On/Off jumper (if removed, power to motor is cut).
